// Logisim project mata3820171.circ as structural Verilog
module main (
  input  [7:0] E3,
  input  [7:0] E2,
  input  [7:0] E1,
  input  [7:0] E0,
  input  [1:0] in_5,
  input  [1:0] in_6,
  output [7:0] out_7,
  output [7:0] out_8,
  output [7:0] out_9,
  output [7:0] out_10,
  output [7:0] out_11,
  output [7:0] out_12,
  output [7:0] out_13,
  output [7:0] out_14,
  output [7:0] out_15,
  output [7:0] out_16,
  output [7:0] out_17,
  output [7:0] out_18,
  output [7:0] out_19,
  output [7:0] out_20,
  output [7:0] out_21,
  output [7:0] out_22,
  output [7:0] out_23,
  output [7:0] out_24,
  output [7:0] out_25,
  output [7:0] out_26,
  output [7:0] out_27,
  output [7:0] out_28,
  output [7:0] out_29,
  output [7:0] out_30,
  output [7:0] out_31,
  output [7:0] out_32,
  output out_33,
  output [7:0] out_34,
  output [7:0] out_35,
  output out_36,
  output [7:0] out_37,
  output [7:0] out_38,
  output [7:0] out_39,
  output [7:0] out_40,
  output [7:0] out_41,
  output out_42,
  output [7:0] out_43,
  output [7:0] out_44,
  output [7:0] out_45,
  output out_46,
  output [7:0] out_47,
  output [7:0] out_48,
  output out_49,
  output [7:0] out_50,
  output [7:0] out_51,
  output [7:0] out_52,
  output [7:0] out_53
);

  wire adder_1_cout, clock_1_out, comparator_4_eq, comparator_4_lt, comparator_5_eq, comparator_5_gt,
       undriven;
  wire [7:0] multiplexer_1_out, multiplexer_2_out, multiplexer_3_out;
  wire [7:1] undriven_2, undriven_3, undriven_4, undriven_5, undriven_6;

  Clock clock_1 (.out(clock_1_out));
  Multiplexer #(.select(2), .width(8)) multiplexer_1 (
    .in0(out_10), .in1(out_9), .in2(out_8), .in3(out_7), .out(multiplexer_1_out), .sel(in_5));  // open: en
  Register R1 (.D(E1), .Q(out_9), .clk(clock_1_out));  // open: en, clr
  Register R0 (.D(multiplexer_3_out), .en(undriven), .Q(out_10), .clk(clock_1_out));  // open: clr
  Register R2 (.D(E2), .Q(out_8), .clk(clock_1_out));  // open: en, clr
  Register R3 (.D(E3), .Q(out_7), .clk(clock_1_out));  // open: en, clr
  Multiplexer #(.select(2), .width(8)) multiplexer_2 (
    .in0(out_10), .in1(out_9), .in2(out_8), .in3(out_7), .out(multiplexer_2_out), .sel(in_6));  // open: en
  Demultiplexer #(.select(4), .width(8)) demultiplexer_1 (
    .out0(out_12), .out1(out_13), .out2(out_15), .out3(out_16), .out4(out_17), .out5(out_19), .out6(out_20),
    .out7(out_22), .out8(out_23), .out9(out_24), .out10(out_26), .out11(out_27), .out12(out_28),
    .out13(out_28), .out14(out_28), .out15(out_28), .in(multiplexer_1_out), .sel(4'b1010));  // open: en
  Demultiplexer #(.select(4), .width(8)) demultiplexer_2 (
    .out0(out_34), .out1(out_35), .out2(out_37), .out3(out_38), .out4(out_39), .out5(out_40), .out6(out_41),
    .out7(out_43), .out8(out_44), .out9(out_45), .out10(out_47), .out11(out_48), .out12(out_50),
    .out13(out_51), .out14(out_52), .out15(out_53), .in(multiplexer_2_out), .sel(4'b1010));  // open: en
  assign out_11 = out_13 & out_34;  // AND_Gate and_1, 8 bits wide
  assign out_14 = out_12 | out_35;  // OR_Gate or_1, 8 bits wide
  assign out_18 = out_15 ^ out_37;  // XOR_Gate xor_1, 8 bits wide
  assign out_21 = ~out_16;  // NOT_Gate not_1, 8 bits wide
  Adder adder_1 (.a(out_17), .b(out_39), .out(out_25), .cout(adder_1_cout));  // open: cin
  Subtractor subtractor_1 (.a(out_19), .b(out_40), .out(out_29));  // open: bin, bout
  Comparator comparator_1 (.a(out_20), .b(out_41), .eq(out_33));  // open: gt, lt
  Comparator comparator_2 (.a(out_22), .b(out_44), .lt(out_36));  // open: gt, eq
  Comparator comparator_3 (.a(out_24), .b(out_44), .eq(out_42));  // open: gt, lt
  Comparator comparator_4 (.a(out_26), .b(out_45), .eq(comparator_4_eq), .lt(comparator_4_lt));  // open: gt
  Comparator comparator_5 (.a(out_28), .b(out_47), .gt(comparator_5_gt), .eq(comparator_5_eq));  // open: lt
  Multiplexer #(.select(4), .width(8)) multiplexer_3 (
    .in0(out_11), .in1(out_14), .in2(out_18), .in3(out_21), .in4(out_25), .in5(out_29),
    .in6({undriven_2, out_33}), .in7({undriven_4, out_36}), .in8({undriven_3, out_42}),
    .in9({undriven_5, out_46}), .in10({undriven_6, out_49}), .out(multiplexer_3_out), .sel(4'b1010));  // open: in11, in12, in13, in14, in15, en
  or or_2 (out_46, comparator_4_eq, comparator_4_lt);
  or or_3 (out_49, comparator_5_gt, comparator_5_eq);
  // Pins of 1 and 8 bits meet at {undriven_6, out_49}
  // Pins of 1 and 8 bits meet at {undriven_3, out_42}
  // Pins of 1 and 8 bits meet at {undriven_4, out_36}
  // Pins of 1 and 8 bits meet at {undriven_5, out_46}
  // Pins of 1 and 8 bits meet at {undriven_2, out_33}

  assign out_30 = out_28;
  assign out_31 = out_28;
  assign out_32 = out_28;

  // Notes on the sheet:
  //   Rx
  //   Ry
endmodule
