// Logisim project memoria.circ as structural Verilog: 1 circuit, main circuit main
module main (
  input  Teste_igualdade,
  input  [15:0] Adiciona_um_valor_ao_contador,
  input  clear,
  input  seletor_de_bit,
  output [15:0] out_5,
  output Indica_se_terminou_a_contagem,
  output [7:0] out_7,
  output [7:0] out_8
);

  wire \_0_armazena__1_lê_out , clock_1_out, comparator_1_eq, not_1_out;

  Counter #(.width(16), .max('hffff), .ongoal("stay")) counter_1 (
    .load(Teste_igualdade), .D(Adiciona_um_valor_ao_contador), .Q(out_5),
    .carry(Indica_se_terminou_a_contagem), .clk(clock_1_out), .clr(clear));  // open: count
  Clock clock_1 (.out(clock_1_out));
  BitSelector #(.width(16), .group(8)) bitselector_1 (.in(out_5), .out(out_8), .sel(seletor_de_bit));
  Comparator #(.mode("unsigned")) comparator_1 (.a(out_8), .b(out_7), .eq(comparator_1_eq));  // open: gt, lt
  not not_1 (not_1_out, comparator_1_eq);
  LED \Entrada_e_saída_iguais  (.in(not_1_out));
  not \_0_armazena__1_lê  (\_0_armazena__1_lê_out , Indica_se_terminou_a_contagem);
  RAM #(.addrWidth(16), .bus("separate")) ram_1 (
    .addr(out_5), .din(out_8), .data(out_7), .str(\_0_armazena__1_lê_out ), .clk(clock_1_out));  // open: sel, ld, clr

  // Notes on the sheet:
  //   endereçamento
  //   entrada de dados
endmodule
